# Fritzing sketch GPS_ESP32 (saved by Fritzing 0.9.3b)

parts:
  GPS_GY-NEO6MV2 = SUP500F [package=sup500f]
  MH-ET_LIVE_ESP32_DEVKIT1 = MH-ET LIVE ESP32 DEVKIT 38 pins

nets:
  N1: GPS_GY-NEO6MV2.RX-I, MH-ET_LIVE_ESP32_DEVKIT1.CMD
  N2: GPS_GY-NEO6MV2.TX-O, MH-ET_LIVE_ESP32_DEVKIT1.TXD0
  N3: GPS_GY-NEO6MV2.GND, MH-ET_LIVE_ESP32_DEVKIT1.IO22
  N4: GPS_GY-NEO6MV2.VCC, MH-ET_LIVE_ESP32_DEVKIT1.SCK

notes:
  GND Marron
  TX Naranja
  RX Amarillo
  VCC Rojo
  3,3v

custom parts:
  MH-ET LIVE ESP32 DEVKIT 38 pins: http://mh.nodebb.com/topic/2/mh-et-live-esp32-devkit
