# Fritzing sketch OLED_ESP32 (saved by Fritzing 0.9.3b)

parts:
  MH-ET_LIVE_ESP32_DEVKIT1 = MH-ET LIVE ESP32 DEVKIT 38 pins
  Grove1 = Grove OLED 128x96

nets:
  5V: MH-ET_LIVE_ESP32_DEVKIT1.5V, Grove1.VCC
  N1: MH-ET_LIVE_ESP32_DEVKIT1.IO23, Grove1.SDA
  N2: MH-ET_LIVE_ESP32_DEVKIT1.RXD0, Grove1.SCL
  N3: MH-ET_LIVE_ESP32_DEVKIT1.SD0, Grove1.GND

notes:
  #include <Wire.h>
  #include <U8g2lib.h>
  #define OLED_ADDRESS 0x3C
  U8G2_SSD1306_128X64_NONAME_F_HW_I2C u8g2(U8G2_R0, /* reset=*/ U8X8_PIN_NONE);
  void setup() {
  Wire.begin(21, 22); // Inicializar la comunicación I2C con los pines GPIO21 (SCL) y GPIO22 (SDA)
  u8g2.begin(); // Inicializar la pantalla OLED
  u8g2.setFlipMode(1); // Girar la pantalla si es necesario (0 = no girar, 1 = girar)
  Serial.begin(115200); // Inicializar el Monitor Serie
  while (!Serial); // Esperar a que se establezca la conexión serial
  }
  void loop() {
  u8g2.clearBuffer(); // Limpiar el buffer de la pantalla
  u8g2.setFont(u8g2_font_ncenB10_tr); // Establecer la fuente
  u8g2.drawStr(0, 15, "....ES DE 15...."); // Mostrar texto en la pantalla
  u8g2.sendBuffer(); // Enviar el contenido del buffer a la pantalla
  Serial.println("ABCDEFGHIJKLMN"); // Imprimir texto en el Monitor Serie
  delay(2000); // Esperar 2 segundos
  u8g2.clearBuffer(); // Limpiar el buffer de la pantalla
  u8g2.setFont(u8g2_font_ncenB10_tr); // Establecer la fuente
  u8g2.drawStr(0, 60, "----ES DE 60----"); // Mostrar texto en la pantalla
  u8g2.sendBuffer(); // Enviar el contenido del buffer a la pantalla
  Serial.println("ABCDEFGHIJKLMN"); // Imprimir texto en el Monitor Serie
  delay(2000); // Esperar 2 segundos
  }

custom parts:
  MH-ET LIVE ESP32 DEVKIT 38 pins: http://mh.nodebb.com/topic/2/mh-et-live-esp32-devkit
